# Fritzing sketch WeatherStationNodeMCU (saved by Fritzing 0.9.3b)
breadboards: 1

parts:
  U1 = NodeMCU V1.0
  Componente1 = Real Time Clock Module - DS1307 RTC Breakout Board
  Componente2 = Barometric Pressure Sensor - BMP085 Breakout

nets:
  N1: U1.D1, Componente1.SCL, Componente2.SCL
  N2: U1.D2, Componente1.SDA, Componente2.SDA
  GND: U1.GND#13, Componente1.GND, Componente2.GND
  5V: U1.3V3#14, Componente1.5V, Componente2.VCC

custom parts:
  NodeMCU V1.0: ESP8266 based NodeMCU V1.0
